# Fritzing sketch accelrelay (saved by Fritzing 0.9.2b)
breadboards: 1

parts:
  Part1 = Arduino Uno (Rev3)
  U2 = 2-Channel 5v Relay Shield [package=relay-2ch5v10a]
  R1 = Resistor [tolerance=±5% resistance=220 package=THT]
  Part2 = Triple Axis Accelerometer Breakout - ADXL335

nets:
  N1: Part1.A0, Part2.ZOUT
  N2: Part1.A1, Part2.YOUT
  N3: Part1.A2, Part2.XOUT
  VCC: Part1.AREF, Part1.3V3, U2.VCC, Part2.VCC
  N4: Part1.D2, U2.IN1
  GND: Part1.GND, U2.GND, U2.K1-In
  N5: U2.K1-On, R1.Pin_0
  N6: R1.Pin_1, Part2.GND

notes:
  Match pin labels- Ignore: ST, red dot on breadboard

custom parts:
  2-Channel 5v Relay Shield: 2 Channel 5v Relay Shield w. 2x SPD-06VDC-SD-C
