# Fritzing sketch accelrelayrf (saved by Fritzing 0.9.2b)
breadboards: 2

parts:
  Part1 = Arduino Uno (Rev3)
  U2 = 2-Channel 5v Relay Shield [package=relay-2ch5v10a]
  R1 = Resistor [tolerance=±5% resistance=220 package=THT]
  Part2 = Triple Axis Accelerometer Breakout - ADXL335
  U3 = RF-LINK_TX [package=rf-link_tx]
  Part3 = Arduino Uno (Rev3)
  U4 = RF-LINK_RX [package=rf-link_rx]

nets:
  N1: Part1.A0, Part2.ZOUT
  N2: Part1.A1, Part2.YOUT
  N3: Part1.A2, Part2.XOUT
  N4: Part1.D12/MISO, U3.GND
  GND: Part1.GND, U2.GND, U2.K1-In, U3.ANT
  VCC: Part1.AREF, Part1.3V3, U2.VCC, Part2.VCC
  N5: Part1.D2, U2.IN1
  5V: Part1.5V, U3.+5V
  N6: U2.K1-On, R1.Pin_0
  N7: R1.Pin_1, Part2.GND
  N8: Part3.GND, U4.ANT

notes:
  Match pin labels- Ignore: ST, red dot on breadboard, Transmitter + Receiver extra pin

custom parts:
  2-Channel 5v Relay Shield: 2 Channel 5v Relay Shield w. 2x SPD-06VDC-SD-C
