# Fritzing sketch ledtwochannel (saved by Fritzing 0.9.2b)
breadboards: 1

parts:
  Part1 = Arduino Uno (Rev3)
  U2 = 2-Channel 5v Relay Shield [package=relay-2ch5v10a]
  LED1 = smd LED [color="Red (633nm)" package="1206 [SMD]"]
  R1 = Resistor [tolerance=±5% resistance=220 package=THT]

nets:
  GND: Part1.GND, U2.GND, U2.K1-In
  N1: Part1.D2, U2.IN1
  N2: Part1.D3_PWM, LED1.cathode
  5V: Part1.5V, U2.VCC
  N3: U2.K1-On, R1.Pin_0
  N4: LED1.anode, R1.Pin_1

custom parts:
  2-Channel 5v Relay Shield: 2 Channel 5v Relay Shield w. 2x SPD-06VDC-SD-C
